# Fritzing sketch InitialSketch (saved by Fritzing 0.9.3b)
breadboards: 1

parts:
  S1 = Toggle Switch [package=THT]
  R1 = Resistor [tolerance=±5% resistance=220 package=THT]
  Raspberry_Pi_1 = Raspberry Pi 3 [part_number=RPI-3-V1.2]
  R2 = Resistor [tolerance=±5% resistance=220 package="1206 [SMD]"]
  S2 = Toggle Switch [package=THT]
  R3 = Resistor [tolerance=±5% resistance=220 package=THT]
  R4 = Resistor [tolerance=±5% resistance=220 package="1206 [SMD]"]
  S3 = Toggle Switch [package=THT]
  R5 = Resistor [tolerance=±5% resistance=220 package=THT]
  R6 = Resistor [tolerance=±5% resistance=220 package="1206 [SMD]"]
  S4 = Toggle Switch [package=THT]
  R7 = Resistor [tolerance=±5% resistance=220 package=THT]
  R8 = Resistor [tolerance=±5% resistance=220 package="1206 [SMD]"]

nets:
  N1: S1.L1, Raspberry_Pi_1.3v3, S2.L1, S3.L1, S4.L1
  N2: S1.L2, R1.Pin_1
  N3: R1.Pin_0, Raspberry_Pi_1.GPIO8, R2.Pin_0
  N4: Raspberry_Pi_1.GPIO17, R7.Pin_0, R8.Pin_0
  N5: Raspberry_Pi_1.GPIO7, R3.Pin_0, R4.Pin_0
  N6: Raspberry_Pi_1.GPIO18, R5.Pin_0, R6.Pin_0
  N7: Raspberry_Pi_1.GND, R2.Pin_1, R4.Pin_1, R6.Pin_1, R8.Pin_1
  N8: S2.L2, R3.Pin_1
  N9: S3.L2, R5.Pin_1
  N10: S4.L2, R7.Pin_1
